// Logisim project cpu.circ as structural Verilog: 1 circuit, main circuit main
module main (
  input  in_1
);

  wire ADC_OR_SBB_out, adder_1_cout, and_1_out, and_2_out, and_3_out, and_4_out, and_5_out, and_6_out,
       and_8_out, and_9_out, and_10_out, and_11_out, and_12_out, and_13_out, and_14_out, and_15_out,
       and_16_out, and_17_out, and_18_out, and_19_out, and_20_out, and_21_out, and_22_out, and_23_out,
       and_24_out, and_25_out, and_26_out, and_27_out, and_28_out, and_29_out, and_30_out, and_31_out,
       and_32_out, and_33_out, and_34_out, and_35_out, and_36_out, and_37_out, and_38_out, and_39_out,
       and_40_out, buffer_1_out, buffer_2_out, buffer_3_out, buffer_4_out, buffer_5_out, buffer_6_out,
       buffer_7_out, buffer_8_out, buffer_9_out, BYTE_SRC_out, CLK, CMP_OR_SUB_out, d_ff_1_q, d_ff_2_q,
       d_ff_3_q, d_ff_4_q, d_ff_5_q, d_ff_6_q, d_ff_6_qn, d_ff_7_q, decoder_1_out0, decoder_1_out1,
       decoder_1_out2, decoder_1_out3, decoder_1_out4, decoder_1_out5, decoder_1_out6, decoder_1_out7,
       decoder_1_out9, decoder_1_out10, decoder_1_out11, decoder_1_out12, decoder_2_out0, decoder_2_out1,
       decoder_2_out5, decoder_2_out6, decoder_2_out7, decoder_2_out8, decoder_2_out9, decoder_2_out15,
       decoder_3_out0, decoder_3_out1, decoder_3_out2, decoder_3_out3, decoder_3_out4, decoder_3_out5,
       decoder_3_out6, decoder_3_out7, decoder_3_out8, decoder_3_out9, decoder_3_out10, decoder_4_out0,
       decoder_4_out1, decoder_4_out2, decoder_4_out3, decoder_4_out4, decoder_4_out5, decoder_4_out7,
       decoder_4_out8, decoder_4_out9, decoder_4_out10, decoder_4_out12, decoder_5_out0, decoder_5_out1,
       decoder_5_out2, decoder_5_out3, decoder_5_out4, decoder_5_out5, decoder_5_out6, decoder_5_out7,
       END_INST_out, END_READ_OR_WRITE_out, FETCHING_INSTRUCTION_out, IO, latch16_2_p3, latch16_2_p4,
       MEM_CLK, MEM_O_EN, MEM_W_EN, MOV_OR_ALU_out, nand_1_out, nor_2_out, not_1_out, not_2_out, not_3_out,
       not_5_out, not_6_out, not_7_out, not_8_out, or_1_out, or_2_out, or_3_out, or_4_out, or_6_out,
       or_7_out, or_8_out, or_9_out, or_10_out, or_11_out, or_12_out, or_13_out, or_14_out, or_15_out,
       or_16_out, or_17_out, or_18_out, or_19_out, or_20_out, or_21_out, or_22_out, or_23_out, or_24_out,
       or_25_out, or_26_out, or_27_out, or_28_out, or_29_out, or_30_out, or_33_out, s_r_ff_1_q, s_r_ff_2_q,
       SAME_SIGN_out, subtractor_1_bout, trigger_1_q, trigger_2_q, trigger_3_q, trigger_4_q, trigger_5_q,
       trigger_6_q, trigger_7_q, trigger_8_q, trigger_9_q, trigger_10_q, trigger_11_q, trigger_12_q,
       trigger_13_q, trigger_14_q, trigger_15_q, trigger_16_q, trigger_17_q, trigger_18_q, undriven_2,
       WIDE_OPCODE_q, WIDE_OPCODE_READ_out, xnor_1_out, xor_1_out, xor_3_out, xor_4_out, xor_5_out, xor_6_out;
  wire [0:0] shift_register_1_p5;
  wire [1:0] controlled_buffer_18_out;
  wire [1:1] FLAGS_q_2;
  wire [2:0] UOP_ROM_data_4;
  wire [3:0] ARG_LATCH_q, ARG_LATCH_q_2, counter_1_q, latch16_2_p6, latch16_3_q, latch16_4_q,
       multiplexer_2_out, multiplexer_3_out, multiplexer_4_out, nor_1_out, undriven, UOP_ROM_data_2,
       UOP_ROM_data_3;
  wire [4:0] UOP_ROM_data;
  wire [6:0] FLAGS_q, xor_2_out, xor_2_out_3;
  wire [7:0] ACC_H_q, ACC_L_q, controlled_buffer_22_out, controlled_buffer_25_out, controlled_buffer_27_out,
       controlled_buffer_32_out, DATA, latch8_1_q, latch8_2_q, multiplexer_5_out, OPCODE_LATCH_q,
       register_1_q;
  wire [11:0] latch16_2_p6_2, latch16_3_q_2, latch16_4_q_2, multiplexer_4_out_2;
  wire [14:0] shift_register_2_p11;
  wire [15:0] adder_1_out, adder_2_out, adder_3_out, adder_4_out, ADDRESS, ALU_IN_LATCH_q, ALU_OUT_LATCH_q,
       and_7_out, BASE_q, controlled_buffer_1_out, controlled_buffer_3_out, controlled_buffer_9_out,
       controlled_buffer_15_out, controlled_buffer_20_out, controlled_buffer_30_out,
       controlled_buffer_31_out, controlled_buffer_34_out, divider_1_out, IP_q, latch16_1_q,
       multiplexer_1_out, multiplexer_6_out, multiplier_1_out, or_5_out, PREV_IP_q, shifter_1_out,
       shifter_2_out, STB_q, STT_q, subtractor_1_out;
  wire [15:7] xor_2_out_2;

  Decoder #(.select(4)) decoder_1 (
    .out0(decoder_1_out0), .out1(decoder_1_out1), .out2(decoder_1_out2), .out3(decoder_1_out3),
    .out4(decoder_1_out4), .out5(decoder_1_out5), .out6(decoder_1_out6), .out7(decoder_1_out7),
    .out9(decoder_1_out9), .out10(decoder_1_out10), .out11(decoder_1_out11), .out12(decoder_1_out12),
    .sel(UOP_ROM_data_3), .en(decoder_2_out5));  // open: out8, out13, out14, out15
  not not_1 (not_1_out, decoder_2_out5);
  buf buffer_1 (buffer_1_out, decoder_2_out5);
  nor FETCHING_INSTRUCTION (FETCHING_INSTRUCTION_out, OPCODE_LATCH_q[0], OPCODE_LATCH_q[1], OPCODE_LATCH_q[2], OPCODE_LATCH_q[3], OPCODE_LATCH_q[4], OPCODE_LATCH_q[5], OPCODE_LATCH_q[6], OPCODE_LATCH_q[7]);
  or or_1 (or_1_out, buffer_2_out, END_INST_out);
  xor xor_1 (xor_1_out, CLK, d_ff_1_q);
  D_Flip_Flop d_ff_1 (.D(and_1_out), .clk(or_7_out), .Q(d_ff_1_q), .reset(in_1));  // open: Qn, preset
  and and_1 (and_1_out, CLK, d_ff_2_q);
  D_Flip_Flop d_ff_2 (.D(1'b1), .clk(CLK), .Q(d_ff_2_q), .reset(or_1_out));  // open: Qn, preset
  Register #(.width(16)) ALU_IN_LATCH (
    .D(controlled_buffer_15_out), .en(1'b1), .clk(trigger_1_q), .Q(ALU_IN_LATCH_q));  // open: clr
  trigger trigger_1 (.Q(trigger_1_q), .CLK(and_2_out));
  and and_2 (and_2_out, decoder_2_out1, decoder_3_out7);
  assign controlled_buffer_1_out = not_1_out ? {16{1'b0}} : 16'bz;  // Controlled_Buffer controlled_buffer_1
  assign controlled_buffer_1_out = buffer_1_out ? controlled_buffer_15_out : 16'bz;  // Controlled_Buffer controlled_buffer_2
  or ADC_OR_SBB (ADC_OR_SBB_out, decoder_1_out12, decoder_1_out11);
  or END_INST (END_INST_out, in_1, and_20_out, decoder_2_out0);
  not not_2 (not_2_out, xor_1_out);
  Register OPCODE_LATCH (
    .D(controlled_buffer_15_out[7:0]), .en(1'b1), .clk(buffer_2_out), .Q(OPCODE_LATCH_q), .clr(END_INST_out));
  Register ARG_LATCH (
    .D(controlled_buffer_15_out[15:8]), .en(1'b1), .clk(buffer_2_out), .Q({ARG_LATCH_q_2, ARG_LATCH_q}),
    .clr(END_INST_out));
  or or_2 (or_2_out, or_1_out, or_7_out);
  // Shift_Register shift_register_1: pin names not known; wires that end beside it: or_2_out, 1'b1, xor_1_out, 1'b1, shift_register_1_p5[0], shift_register_2_p11[1]
  // Shift_Register shift_register_2: pin names not known; wires that end beside it: or_2_out, 1'b1, not_2_out, 1'b1, shift_register_2_p11[3], shift_register_2_p11[5], shift_register_2_p11[7], shift_register_2_p11[9], shift_register_2_p11[11], shift_register_2_p11[13], shift_register_2_p11[0], shift_register_2_p11[2], shift_register_2_p11[4], shift_register_2_p11[6], shift_register_2_p11[8], shift_register_2_p11[10], shift_register_2_p11[12], shift_register_2_p11[14]
  trigger trigger_2 (.Q(trigger_2_q), .CLK(trigger_3_q));
  trigger trigger_3 (.Q(trigger_3_q), .CLK(decoder_2_out15));
  assign controlled_buffer_3_out = decoder_1_out0 ? adder_1_out : 16'bz;  // Controlled_Buffer controlled_buffer_3
  Adder #(.width(16)) adder_1 (
    .a(ALU_IN_LATCH_q), .b(controlled_buffer_1_out), .out(adder_1_out), .cin(and_3_out), .cout(adder_1_cout));
  Subtractor #(.width(16)) subtractor_1 (
    .a(ALU_IN_LATCH_q), .b(controlled_buffer_1_out), .out(subtractor_1_out), .bin(and_3_out),
    .bout(subtractor_1_bout));
  assign controlled_buffer_3_out = decoder_1_out2 ? multiplier_1_out : 16'bz;  // Controlled_Buffer controlled_buffer_4
  Multiplier #(.width(16)) multiplier_1 (
    .a(ALU_IN_LATCH_q), .b(controlled_buffer_1_out), .out(multiplier_1_out));  // open: cin, cout
  assign controlled_buffer_3_out = decoder_1_out3 ? divider_1_out : 16'bz;  // Controlled_Buffer controlled_buffer_5
  Divider #(.width(16)) divider_1 (
    .a(ALU_IN_LATCH_q), .b(controlled_buffer_1_out), .out(divider_1_out));  // open: upper, rem
  assign controlled_buffer_3_out = decoder_1_out9 ? shifter_1_out : 16'bz;  // Controlled_Buffer controlled_buffer_6
  Shifter #(.width(16)) shifter_1 (.in(ALU_IN_LATCH_q), .\dist (controlled_buffer_1_out[3:0]), .out(shifter_1_out));
  assign controlled_buffer_3_out = decoder_1_out10 ? shifter_2_out : 16'bz;  // Controlled_Buffer controlled_buffer_7
  Shifter #(.shift("lr"), .width(16)) shifter_2 (
    .in(ALU_IN_LATCH_q), .\dist (controlled_buffer_1_out[3:0]), .out(shifter_2_out));
  assign controlled_buffer_3_out = not_1_out ? controlled_buffer_1_out : 16'bz;  // Controlled_Buffer controlled_buffer_8
  or CMP_OR_SUB (CMP_OR_SUB_out, decoder_1_out1, decoder_1_out4);
  and and_3 (and_3_out, ADC_OR_SBB_out, FLAGS_q_2[1]);
  S_R_Flip_Flop WIDE_OPCODE (
    .Q(WIDE_OPCODE_q), .reset(or_1_out), .preset(WIDE_OPCODE_READ_out));  // open: S, R, clk, Qn
  assign controlled_buffer_9_out = decoder_2_out1 ? controlled_buffer_15_out : 16'bz;  // Controlled_Buffer controlled_buffer_9
  or or_3 (or_3_out, WIDE_OPCODE_q, UOP_ROM_data_2[0]);
  and and_4 (and_4_out, decoder_2_out1, decoder_3_out4);
  assign controlled_buffer_3_out = CMP_OR_SUB_out ? subtractor_1_out : 16'bz;  // Controlled_Buffer controlled_buffer_10
  buf buffer_2 (buffer_2_out, buffer_3_out);
  S_R_Flip_Flop s_r_ff_1 (.Q(s_r_ff_1_q), .reset(and_6_out), .preset(and_5_out));  // open: S, R, clk, Qn
  and and_5 (and_5_out, ~counter_1_q[0], ~counter_1_q[1], ~counter_1_q[2], ~counter_1_q[3]);  // AND_Gate
  and and_6 (and_6_out, ~in_1, or_1_out);  // AND_Gate
  assign controlled_buffer_9_out = decoder_2_out15 ? adder_2_out : 16'bz;  // Controlled_Buffer controlled_buffer_11
  or or_4 (or_4_out, trigger_2_q, and_4_out);
  assign controlled_buffer_3_out = decoder_1_out5 ? and_7_out : 16'bz;  // Controlled_Buffer controlled_buffer_12
  buf buffer_3 (buffer_3_out, decoder_3_out6);
  Register #(.width(16)) IP (.D(controlled_buffer_9_out), .en(1'b1), .clk(trigger_4_q), .Q(IP_q), .clr(in_1));
  trigger trigger_4 (.Q(trigger_4_q), .CLK(or_4_out));
  assign and_7_out = controlled_buffer_1_out & ALU_IN_LATCH_q;  // AND_Gate and_7, 16 bits wide
  assign or_5_out = controlled_buffer_1_out | ALU_IN_LATCH_q;  // OR_Gate or_5, 16 bits wide
  assign controlled_buffer_3_out = decoder_1_out6 ? or_5_out : 16'bz;  // Controlled_Buffer controlled_buffer_13
  assign controlled_buffer_3_out = decoder_1_out7 ? {xor_2_out_2[15], xor_2_out_3, xor_2_out_2[7], xor_2_out} : 16'bz;  // Controlled_Buffer controlled_buffer_14
  nor SAME_SIGN (SAME_SIGN_out, and_8_out, and_12_out);
  and and_8 (and_8_out, xor_2_out_2[15], ~and_18_out);  // AND_Gate
  LATCH16 latch16_1 (.Q(latch16_1_q), .WE(s_r_ff_1_q), .D({undriven, OPCODE_LATCH_q, counter_1_q}));  // open: R
  S_R_Flip_Flop s_r_ff_2 (.Q(s_r_ff_2_q), .reset(or_6_out), .preset(shift_register_1_p5[0]));  // open: S, R, clk, Qn
  or or_6 (or_6_out, in_1, decoder_2_out0, or_1_out);
  Counter #(.max('hf), .width(4)) counter_1 (
    .clr(or_1_out), .up(1'b1), .clk(or_7_out), .Q(counter_1_q));  // open: load, count, D, carry
  or or_7 (or_7_out, trigger_8_q, trigger_5_q, trigger_1_q, trigger_13_q, or_18_out, trigger_6_q, and_19_out, trigger_4_q);
  assign controlled_buffer_15_out = decoder_4_out4 ? IP_q : 16'bz;  // Controlled_Buffer controlled_buffer_15
  assign {xor_2_out_2[15], xor_2_out_3, xor_2_out_2[7], xor_2_out} = controlled_buffer_1_out ^ ALU_IN_LATCH_q;  // XOR_Gate xor_2, 16 bits wide
  and and_9 (and_9_out, decoder_2_out5, shift_register_1_p5[0]);
  trigger trigger_5 (.Q(trigger_5_q), .CLK(and_9_out));
  and and_10 (and_10_out, ALU_IN_LATCH_q[7], and_18_out);
  and and_11 (and_11_out, ~and_18_out, ALU_IN_LATCH_q[15]);  // AND_Gate
  and and_12 (and_12_out, xor_2_out_2[7], and_18_out);
  ROM #(.addrWidth(12), .dataWidth(16)) UOP_ROM (
    .addr(latch16_1_q[11:0]), .data({UOP_ROM_data_3, UOP_ROM_data_2, UOP_ROM_data_4, UOP_ROM_data}));
  Multiplexer #(.width(16)) multiplexer_1 (.in0(16'h1), .in1(16'h2), .out(multiplexer_1_out), .sel(or_3_out));
  and and_13 (and_13_out, trigger_5_q, UOP_ROM_data[4]);
  xor xor_3 (xor_3_out, CMP_OR_SUB_out, SAME_SIGN_out);
  or or_8 (or_8_out, and_10_out, and_11_out);
  or NEGATIVE (nor_1_out[2], and_14_out, and_15_out);
  and and_14 (and_14_out, controlled_buffer_3_out[15], ~and_18_out);  // AND_Gate
  and and_15 (and_15_out, controlled_buffer_3_out[7], and_18_out);
  Adder #(.width(16)) adder_2 (.a(multiplexer_1_out), .b(IP_q), .out(adder_2_out));  // open: cin, cout
  Register #(.width(16)) PREV_IP (.D(IP_q), .en(1'b1), .clk(trigger_4_q), .Q(PREV_IP_q), .clr(in_1));
  Register #(.width(16)) ALU_OUT_LATCH (
    .D(controlled_buffer_3_out), .en(1'b1), .clk(trigger_5_q), .Q(ALU_OUT_LATCH_q));  // open: clr
  Register FLAGS (
    .D({4'b0000, nor_1_out}), .en(1'b1), .clk(and_13_out), .Q({FLAGS_q[6:1], FLAGS_q_2[1], FLAGS_q[0]}));  // open: clr
  and OVERFLOW (nor_1_out[3], xor_3_out, xor_4_out);
  xor xor_4 (xor_4_out, or_8_out, nor_1_out[2]);
  or CARRY (nor_1_out[1], and_16_out, and_17_out);
  and and_16 (and_16_out, controlled_buffer_3_out[8], and_18_out);
  Decoder #(.select(4)) decoder_2 (
    .out0(decoder_2_out0), .out1(decoder_2_out1), .out3(MEM_W_EN), .out4(MEM_O_EN), .out5(decoder_2_out5),
    .out6(decoder_2_out6), .out7(decoder_2_out7), .out8(decoder_2_out8), .out9(decoder_2_out9),
    .out15(decoder_2_out15), .sel(UOP_ROM_data[3:0]), .en(s_r_ff_2_q));  // open: out2, out10, out11, out12, out13, out14
  assign controlled_buffer_15_out = decoder_4_out12 ? PREV_IP_q : 16'bz;  // Controlled_Buffer controlled_buffer_16
  assign controlled_buffer_15_out = decoder_4_out7 ? ALU_OUT_LATCH_q : 16'bz;  // Controlled_Buffer controlled_buffer_17
  nor nor_1 (nor_1_out[0], controlled_buffer_3_out[0], controlled_buffer_3_out[1], controlled_buffer_3_out[2], controlled_buffer_3_out[3], controlled_buffer_3_out[4], controlled_buffer_3_out[5], controlled_buffer_3_out[6], controlled_buffer_3_out[7], controlled_buffer_3_out[9], controlled_buffer_3_out[10], controlled_buffer_3_out[11], controlled_buffer_3_out[12], controlled_buffer_3_out[13], controlled_buffer_3_out[14], controlled_buffer_3_out[15], controlled_buffer_3_out[8]);
  and and_17 (and_17_out, ~and_18_out, or_9_out);  // AND_Gate
  or or_9 (or_9_out, subtractor_1_bout, adder_1_cout);
  buf buffer_4 (buffer_4_out, decoder_2_out1);
  buf buffer_5 (buffer_5_out, buffer_4_out);
  buf buffer_6 (buffer_6_out, buffer_5_out);
  buf buffer_7 (buffer_7_out, buffer_6_out);
  Decoder #(.select(4)) decoder_3 (
    .out0(decoder_3_out0), .out1(decoder_3_out1), .out2(decoder_3_out2), .out3(decoder_3_out3),
    .out4(decoder_3_out4), .out5(decoder_3_out5), .out6(decoder_3_out6), .out7(decoder_3_out7),
    .out8(decoder_3_out8), .out9(decoder_3_out9), .out10(decoder_3_out10), .sel(multiplexer_2_out),
    .en(buffer_7_out));  // open: out11, out12, out13, out14, out15
  Multiplexer #(.select(2), .width(4)) multiplexer_2 (
    .in0(UOP_ROM_data_3), .in1(ARG_LATCH_q_2), .in2(ARG_LATCH_q), .out(multiplexer_2_out),
    .sel(UOP_ROM_data_4[2:1]));  // open: in3
  buf buffer_8 (buffer_8_out, decoder_2_out1);
  or BYTE_SRC (BYTE_SRC_out, decoder_4_out0, decoder_4_out1);
  assign controlled_buffer_18_out = buffer_8_out ? {UOP_ROM_data_4[0], UOP_ROM_data[4]} : 2'bz;  // Controlled_Buffer controlled_buffer_18
  not not_3 (not_3_out, decoder_2_out1);
  assign controlled_buffer_18_out = not_3_out ? 2'b00 : 2'bz;  // Controlled_Buffer controlled_buffer_19
  or MOV_OR_ALU (MOV_OR_ALU_out, decoder_2_out1, decoder_2_out5);
  and and_18 (and_18_out, BYTE_SRC_out, MOV_OR_ALU_out);
  and WIDE_OPCODE_READ (WIDE_OPCODE_READ_out, ~and_22_out, FETCHING_INSTRUCTION_out, trigger_7_q);  // AND_Gate
  Multiplexer #(.select(2), .width(4)) multiplexer_3 (
    .in0(UOP_ROM_data_2), .in1(ARG_LATCH_q_2), .in2(ARG_LATCH_q), .out(multiplexer_3_out),
    .sel(controlled_buffer_18_out));  // open: in3
  Decoder #(.select(4)) decoder_4 (
    .out0(decoder_4_out0), .out1(decoder_4_out1), .out2(decoder_4_out2), .out3(decoder_4_out3),
    .out4(decoder_4_out4), .out5(decoder_4_out5), .out7(decoder_4_out7), .out8(decoder_4_out8),
    .out9(decoder_4_out9), .out10(decoder_4_out10), .out12(decoder_4_out12), .sel(multiplexer_3_out),
    .en(MOV_OR_ALU_out));  // open: out6, out11, out13, out14, out15
  and and_19 (and_19_out, decoder_3_out5, trigger_9_q);
  trigger trigger_6 (.Q(trigger_6_q), .CLK(END_READ_OR_WRITE_out));
  or END_READ_OR_WRITE (END_READ_OR_WRITE_out, or_11_out, or_12_out);
  trigger trigger_7 (.Q(trigger_7_q), .CLK(latch16_2_p6[0]));
  and and_20 (and_20_out, nor_2_out, trigger_8_q);
  assign controlled_buffer_20_out = decoder_3_out5 ? controlled_buffer_15_out : 16'bz;  // Controlled_Buffer controlled_buffer_20
  assign controlled_buffer_20_out = or_10_out ? adder_3_out : 16'bz;  // Controlled_Buffer controlled_buffer_21
  or or_10 (or_10_out, latch16_2_p6[0], latch16_3_q[0]);
  or or_11 (or_11_out, decoder_2_out9, latch16_3_q[1], latch16_2_p6[1]);
  or or_12 (or_12_out, and_21_out, and_22_out);
  and and_21 (and_21_out, ~UOP_ROM_data_2[0], ~FETCHING_INSTRUCTION_out, or_13_out);  // AND_Gate
  and and_22 (and_22_out, FETCHING_INSTRUCTION_out, latch16_2_p6[0], nand_1_out);
  or or_13 (or_13_out, MEM_W_EN, MEM_O_EN);
  D_Flip_Flop d_ff_3 (.D(1'b1), .clk(MEM_O_EN), .Q(d_ff_3_q), .reset(or_2_out));  // open: Qn, preset
  or or_14 (or_14_out, decoder_3_out0, decoder_3_out2);
  assign controlled_buffer_22_out = decoder_3_out1 ? controlled_buffer_15_out[7:0] : 8'bz;  // Controlled_Buffer controlled_buffer_22
  assign controlled_buffer_22_out = decoder_3_out2 ? controlled_buffer_15_out[15:8] : 8'bz;  // Controlled_Buffer controlled_buffer_23
  or or_15 (or_15_out, decoder_3_out2, decoder_3_out1);
  trigger trigger_8 (.Q(trigger_8_q), .CLK(trigger_10_q));
  and and_23 (and_23_out, FLAGS_q[0], decoder_5_out0);
  Register #(.width(16)) ADDR_LATCH (
    .D(controlled_buffer_20_out), .en(1'b1), .clk(trigger_9_q), .Q(ADDRESS));  // open: clr
  trigger trigger_9 (.Q(trigger_9_q), .CLK(or_16_out));
  or or_16 (or_16_out, decoder_3_out5, latch16_3_q[0], latch16_2_p6[0]);
  nand nand_1 (nand_1_out, latch8_1_q[7], latch8_1_q[6]);
  and and_24 (and_24_out, decoder_2_out1, or_14_out);
  and and_25 (and_25_out, decoder_2_out1, or_15_out);
  trigger trigger_10 (.Q(trigger_10_q), .CLK(decoder_2_out6));
  and and_26 (and_26_out, ~FLAGS_q[0], decoder_5_out1);  // AND_Gate
  and and_27 (and_27_out, ~FLAGS_q_2[1], ~FLAGS_q[0], decoder_5_out2);  // AND_Gate
  assign controlled_buffer_15_out = decoder_4_out5 ? ADDRESS : 16'bz;  // Controlled_Buffer controlled_buffer_24
  Adder #(.width(16)) adder_3 (.a(ADDRESS), .b(16'h1), .out(adder_3_out));  // open: cin, cout
  // LATCH16 latch16_2: pin names not known; wires that end beside it: {shift_register_2_p11, shift_register_1_p5[0]}, d_ff_3_q, latch16_2_p3, latch16_2_p4, latch16_2_p3, {latch16_2_p6_2, latch16_2_p6}
  not not_4 (latch16_2_p4, MEM_O_EN);
  Register ACC_L (.D(controlled_buffer_15_out[7:0]), .en(1'b1), .clk(trigger_11_q), .Q(ACC_L_q));  // open: clr
  trigger trigger_11 (.Q(trigger_11_q), .CLK(and_24_out));
  Register ACC_H (.D(controlled_buffer_22_out), .en(1'b1), .clk(trigger_12_q), .Q(ACC_H_q));  // open: clr
  trigger trigger_12 (.Q(trigger_12_q), .CLK(and_25_out));
  nor nor_2 (nor_2_out, and_23_out, and_26_out, and_27_out, and_28_out, and_29_out, and_32_out, and_34_out, and_36_out);
  and and_28 (and_28_out, or_17_out, decoder_5_out3);
  or or_17 (or_17_out, FLAGS_q[0], FLAGS_q_2[1]);
  Decoder #(.enable("false"), .select(3)) decoder_5 (
    .out0(decoder_5_out0), .out1(decoder_5_out1), .out2(decoder_5_out2), .out3(decoder_5_out3),
    .out4(decoder_5_out4), .out5(decoder_5_out5), .out6(decoder_5_out6), .out7(decoder_5_out7),
    .sel(UOP_ROM_data_2[2:0]));
  D_Flip_Flop d_ff_4 (.D(1'b1), .clk(MEM_W_EN), .Q(d_ff_4_q), .reset(or_2_out));  // open: Qn, preset
  assign controlled_buffer_25_out = not_5_out ? ACC_L_q : 8'bz;  // Controlled_Buffer controlled_buffer_25
  not not_5 (not_5_out, decoder_4_out1);
  assign controlled_buffer_25_out = decoder_4_out1 ? ACC_H_q : 8'bz;  // Controlled_Buffer controlled_buffer_26
  buf buffer_9 (buffer_9_out, decoder_4_out2);
  not not_6 (not_6_out, decoder_4_out2);
  assign controlled_buffer_27_out = buffer_9_out ? ACC_H_q : 8'bz;  // Controlled_Buffer controlled_buffer_27
  assign controlled_buffer_27_out = not_6_out ? {8{1'b0}} : 8'bz;  // Controlled_Buffer controlled_buffer_28
  or or_18 (or_18_out, trigger_16_q, trigger_11_q, trigger_12_q, trigger_17_q, trigger_18_q);
  and and_29 (and_29_out, ~FLAGS_q_2[1], decoder_5_out4);  // AND_Gate
  or or_19 (or_19_out, and_30_out, and_31_out);
  and and_30 (and_30_out, decoder_3_out3, decoder_2_out1);
  and and_31 (and_31_out, or_20_out, or_23_out);
  trigger trigger_13 (.Q(trigger_13_q), .CLK(and_30_out));
  buf or_20 (or_20_out, MEM_O_EN);  // OR_Gate
  LATCH16 latch16_3 (
    .Q({latch16_3_q_2, latch16_3_q}), .WE(d_ff_4_q), .R(not_7_out),
    .D({shift_register_2_p11, shift_register_1_p5[0]}));
  not not_7 (not_7_out, MEM_W_EN);
  assign controlled_buffer_15_out = or_21_out ? {controlled_buffer_27_out, controlled_buffer_25_out} : 16'bz;  // Controlled_Buffer controlled_buffer_29
  or or_21 (or_21_out, decoder_4_out0, decoder_4_out1, decoder_4_out2);
  and and_32 (and_32_out, FLAGS_q_2[1], decoder_5_out5);
  assign controlled_buffer_30_out = decoder_3_out3 ? controlled_buffer_15_out : 16'bz;  // Controlled_Buffer controlled_buffer_30
  or or_22 (or_22_out, and_30_out, and_33_out);
  and and_33 (and_33_out, ~or_23_out, or_20_out);  // AND_Gate
  buf or_23 (or_23_out, latch16_2_p6[0]);  // OR_Gate
  and and_34 (and_34_out, xor_5_out, decoder_5_out6);
  xor xor_5 (xor_5_out, FLAGS_q[2], FLAGS_q[1]);
  buf and_35 (and_35_out, and_33_out);  // AND_Gate
  Multiplexer #(.width(16)) multiplexer_4 (
    .in0({16{1'b0}}), .in1({shift_register_2_p11, shift_register_1_p5[0]}),
    .out({multiplexer_4_out_2, multiplexer_4_out}), .sel(undriven_2));
  trigger trigger_14 (.Q(trigger_14_q), .CLK(decoder_2_out7));
  trigger trigger_15 (.Q(trigger_15_q), .CLK(trigger_14_q));
  and and_36 (and_36_out, xnor_1_out, decoder_5_out7, ~FLAGS_q[0]);  // AND_Gate
  xnor xnor_1 (xnor_1_out, FLAGS_q[2], FLAGS_q[1]);
  LATCH8 latch8_1 (.Q(latch8_1_q), .WE(or_22_out), .D(controlled_buffer_30_out[7:0]));  // open: R
  LATCH8 latch8_2 (.Q(latch8_2_q), .WE(or_19_out), .R(and_35_out), .D(controlled_buffer_30_out[15:8]));
  or or_24 (or_24_out, latch16_2_p6[0], latch16_3_q[0]);
  D_Flip_Flop d_ff_5 (.D(1'b1), .clk(decoder_2_out9), .Q(d_ff_5_q), .reset(or_2_out));  // open: Qn, preset
  assign controlled_buffer_31_out = decoder_3_out9 ? controlled_buffer_15_out : 16'bz;  // Controlled_Buffer controlled_buffer_31
  or or_25 (or_25_out, trigger_15_q, and_37_out);
  and and_37 (and_37_out, decoder_3_out9, decoder_2_out1);
  Multiplexer #(.width(8)) multiplexer_5 (.in0(latch8_1_q), .in1(latch8_2_q), .out(multiplexer_5_out), .sel(or_24_out));
  Demultiplexer #(.disabled("Z"), .tristate("true"), .width(8)) demultiplexer_1 (
    .out0(controlled_buffer_30_out[7:0]), .out1(controlled_buffer_30_out[15:8]),
    .in(controlled_buffer_32_out), .sel(or_24_out));
  assign controlled_buffer_32_out = or_26_out ? DATA : 8'bz;  // Controlled_Buffer controlled_buffer_32
  buf or_26 (or_26_out, MEM_O_EN);  // OR_Gate
  or or_27 (or_27_out, latch16_3_q[1], latch16_2_p6[1]);
  LATCH16 latch16_4 (
    .Q({latch16_4_q_2, latch16_4_q}), .WE(d_ff_5_q), .R(not_8_out),
    .D({shift_register_2_p11, shift_register_1_p5[0]}));
  not not_8 (not_8_out, decoder_2_out9);
  Register #(.width(16)) STT (.D(controlled_buffer_31_out), .en(1'b1), .clk(trigger_16_q), .Q(STT_q));  // open: clr
  assign controlled_buffer_31_out = decoder_2_out7 ? adder_4_out : 16'bz;  // Controlled_Buffer controlled_buffer_33
  trigger trigger_16 (.Q(trigger_16_q), .CLK(or_25_out));
  and and_38 (and_38_out, decoder_2_out1, decoder_3_out10);
  assign controlled_buffer_34_out = decoder_3_out8 ? controlled_buffer_15_out : 16'bz;  // Controlled_Buffer controlled_buffer_34
  and and_39 (and_39_out, decoder_3_out8, decoder_2_out1);
  assign controlled_buffer_15_out = decoder_4_out3 ? {latch8_2_q, latch8_1_q} : 16'bz;  // Controlled_Buffer controlled_buffer_35
  assign DATA = or_28_out ? multiplexer_5_out : 8'bz;  // Controlled_Buffer controlled_buffer_36
  or or_28 (or_28_out, decoder_2_out9, MEM_W_EN);
  or or_29 (or_29_out, latch16_3_q[0], latch16_2_p6[0]);
  Multiplexer #(.width(16)) multiplexer_6 (
    .in0(16'hfffe), .in1(16'h2), .out(multiplexer_6_out), .sel(UOP_ROM_data_2[0]));
  Register #(.width(16)) STB (.D(controlled_buffer_15_out), .en(1'b1), .clk(trigger_17_q), .Q(STB_q));  // open: clr
  trigger trigger_17 (.Q(trigger_17_q), .CLK(and_38_out));
  Register #(.width(16)) BASE (.D(controlled_buffer_34_out), .en(1'b1), .clk(trigger_18_q), .Q(BASE_q));  // open: clr
  trigger trigger_18 (.Q(trigger_18_q), .CLK(and_39_out));
  Clock clock_1 (.out(CLK));
  or or_30 (or_30_out, MEM_O_EN, MEM_W_EN, decoder_2_out9);
  RAM #(.addrWidth(16), .databus("bidir")) ram_1 (
    .addr(ADDRESS), .we(MEM_W_EN), .oe(MEM_O_EN), .clk(MEM_CLK), .data(DATA));
  assign controlled_buffer_15_out = decoder_4_out9 ? STT_q : 16'bz;  // Controlled_Buffer controlled_buffer_37
  Adder #(.width(16)) adder_4 (.a(STT_q), .b(multiplexer_6_out), .out(adder_4_out));  // open: cin, cout
  assign controlled_buffer_15_out = decoder_4_out10 ? STB_q : 16'bz;  // Controlled_Buffer controlled_buffer_38
  assign controlled_buffer_15_out = decoder_4_out8 ? BASE_q : 16'bz;  // Controlled_Buffer controlled_buffer_39
  xor xor_6 (xor_6_out, or_29_out, or_30_out);
  or or_31 (IO, decoder_2_out9, decoder_2_out8);
  or or_32 (MEM_CLK, or_27_out, xor_6_out);
  and and_40 (and_40_out, ~ADDRESS[0], ~ADDRESS[1], ~ADDRESS[2], ~ADDRESS[3], ~ADDRESS[4], ~ADDRESS[5], ~ADDRESS[6], ~ADDRESS[7], ~ADDRESS[8], ~ADDRESS[9], ~ADDRESS[10], ~ADDRESS[11], ~ADDRESS[12], ~ADDRESS[13], ~ADDRESS[14], ~ADDRESS[15], IO);  // AND_Gate
  D_Flip_Flop d_ff_6 (.D(or_33_out), .clk(CLK), .Q(d_ff_6_q), .Qn(d_ff_6_qn), .reset(d_ff_7_q));  // open: preset
  D_Flip_Flop d_ff_7 (.D(d_ff_6_q), .clk(CLK), .Q(d_ff_7_q), .reset(d_ff_7_q));  // open: Qn, preset
  Register register_1 (.D(DATA), .en(and_40_out), .clk(MEM_CLK), .Q(register_1_q), .clr(d_ff_7_q));
  TTY tty_1 (.data(register_1_q[6:0]), .clk(CLK), .we(d_ff_6_qn), .clr(register_1_q[7]));
  or or_33 (or_33_out, register_1_q[0], register_1_q[1], register_1_q[2], register_1_q[3], register_1_q[5], register_1_q[6], register_1_q[7], register_1_q[4]);

  // Other names for the same wires on the sheet: RST = in_1

  // Notes on the sheet:
  //   contents of UOP_ROM (hex, n*v repeats v):
  //   5401 4 f 6301 12*0 5401 4 301 f 12*0 101 15*0 5401 4 1301 f 12*0 1001 15*0 5401 104 2301 10f 12*0
  //   2801 15*0 2901 15*0 2a01 15*0 5401 104 8301 10f 12*0 8201 15*0 8901 15*0 8a01 15*0 5401 104 9301 10f
  //   12*0 9201 15*0 9801 15*0 9a01 15*0 a901 15*0 5401 4 7001 315 701 f 10*0 7001 115 701 13*0 5401 4
  //   7101 315 1701 f 10*0 7101 15 1701 13*0 5401 104 7201 315 2701 10f 10*0 7201 815 2701 13*0 7201 915
  //   2701 13*0 7201 a15 2701 13*0 5401 104 7801 315 8701 10f 10*0 7801 215 8701 13*0 7801 915 8701 13*0
  //   7801 a15 8701 13*0 5401 104 7901 315 9701 10f 10*0 7901 215 9701 13*0 7901 815 9701 77*0 5401 4 7001
  //   1315 701 f 10*0 7001 1115 701 13*0 5401 4 7101 1315 1701 f 10*0 7101 1015 1701 13*0 5401 104 7201
  //   1315 2701 10f 10*0 7201 1815 2701 13*0 7201 1915 2701 13*0 7201 1a15 2701 13*0 5401 104 7801 1315
  //   8701 10f 10*0 7801 1215 8701 13*0 7801 1915 8701 13*0 7801 1a15 8701 13*0 5401 104 7901 1315 9701
  //   10f 10*0 7901 1215 9701 13*0 7901 1815 9701 269*0 5401 4 7001 4315 f 11*0 7001 4115 14*0 5401 4 7101
  //   4315 f 11*0 7101 4015 14*0 5401 104 7201 4315 10f 11*0 7201 4815 14*0 5401 104 7801 4315 10f 11*0
  //   7801 4215 846*0 5401 104 4301 13*0 5401 10f 6 104 4301 11*0 5401 10f 106 104 4301 11*0 5401 10f 206
  //   104 4301 11*0 5401 10f 306 104 4301 11*0 5401 10f 406 104 4301 11*0 5401 10f 506 104 4301 11*0 5401
  //   10f 606 104 4301 11*0 5401 10f 706 104 4301 11*0 5401 104 10f 4301 7 5901 3c01 103 8*0 5901 104 4301
  //   107 12*0 5401 104 7 5901 103 10f 10*0 7 5901 3001 103 12*0 7 5901 3101 103 12*0 7 5901 3201 103 12*0
  //   7 5901 3801 103 12*0 3901 7 5901 103 12*0 7 5901 3a01 103 12*0 5901 107 104 301 12*0 5901 107 104
  //   1301 12*0 5901 107 104 2301 12*0 5901 107 104 8301 12*0 5901 107 104 9301 12*0 5901 107 104 a301
  //   124*0 5801 3001 9 525*0 5401 104 10f 5301 104 341 10*0 5021 104 341 13*0 5401 104 10f 7021 305 5701
  //   104 341 8*0 5401 104 10f 5301 3021 103 10*0 5011 3021 103 13*0 5401 104 10f 7011 305 5701 3021 103
  //   8*0 5401 104 10f 5301 3021 3 10*0 5011 3021 3 13*0 5401 104 10f 7011 305 5701 3021 3
endmodule
