// Logisim project latchb.circ as structural Verilog: 1 circuit, main circuit LATCH8
module LATCH8 (
  input  WE,
  input  R,
  input  [7:0] D,
  output [7:0] Q
);

  wire and_1_out, buffer_2_out, buffer_3_out, buffer_4_out, buffer_5_out, buffer_6_out, buffer_7_out,
       buffer_8_out, buffer_9_out, controlled_inverter_1_out, controlled_inverter_2_out,
       controlled_inverter_3_out, controlled_inverter_4_out, controlled_inverter_5_out,
       controlled_inverter_6_out, controlled_inverter_7_out, controlled_inverter_8_out, or_1_out;
  wire [7:0] buffer_1_out, controlled_buffer_1_out;

  and and_1 (and_1_out, WE, ~R);  // AND_Gate
  assign buffer_1_out = D;  // Buffer buffer_1, 8 bits wide
  assign controlled_buffer_1_out = and_1_out ? buffer_1_out : 8'bz;  // Controlled_Buffer controlled_buffer_1
  assign controlled_buffer_1_out = R ? {8{1'b0}} : 8'bz;  // Controlled_Buffer controlled_buffer_2
  or or_1 (or_1_out, WE, R);
  buf buffer_2 (buffer_2_out, controlled_buffer_1_out[0]);
  S_R_Flip_Flop s_r_ff_1 (.Q(Q[0]), .reset(controlled_inverter_1_out), .preset(buffer_2_out));  // open: S, R, clk, Qn
  assign controlled_inverter_1_out = or_1_out ? ~controlled_buffer_1_out[0] : 1'bz;  // Controlled_Inverter controlled_inverter_1
  buf buffer_3 (buffer_3_out, controlled_buffer_1_out[4]);
  S_R_Flip_Flop s_r_ff_2 (.Q(Q[4]), .reset(controlled_inverter_2_out), .preset(buffer_3_out));  // open: S, R, clk, Qn
  assign controlled_inverter_2_out = or_1_out ? ~controlled_buffer_1_out[4] : 1'bz;  // Controlled_Inverter controlled_inverter_2
  buf buffer_4 (buffer_4_out, controlled_buffer_1_out[1]);
  S_R_Flip_Flop s_r_ff_3 (.Q(Q[1]), .reset(controlled_inverter_3_out), .preset(buffer_4_out));  // open: S, R, clk, Qn
  assign controlled_inverter_3_out = or_1_out ? ~controlled_buffer_1_out[1] : 1'bz;  // Controlled_Inverter controlled_inverter_3
  buf buffer_5 (buffer_5_out, controlled_buffer_1_out[5]);
  S_R_Flip_Flop s_r_ff_4 (.Q(Q[5]), .reset(controlled_inverter_4_out), .preset(buffer_5_out));  // open: S, R, clk, Qn
  assign controlled_inverter_4_out = or_1_out ? ~controlled_buffer_1_out[5] : 1'bz;  // Controlled_Inverter controlled_inverter_4
  buf buffer_6 (buffer_6_out, controlled_buffer_1_out[2]);
  S_R_Flip_Flop s_r_ff_5 (.Q(Q[2]), .reset(controlled_inverter_5_out), .preset(buffer_6_out));  // open: S, R, clk, Qn
  assign controlled_inverter_5_out = or_1_out ? ~controlled_buffer_1_out[2] : 1'bz;  // Controlled_Inverter controlled_inverter_5
  buf buffer_7 (buffer_7_out, controlled_buffer_1_out[6]);
  S_R_Flip_Flop s_r_ff_6 (.Q(Q[6]), .reset(controlled_inverter_6_out), .preset(buffer_7_out));  // open: S, R, clk, Qn
  assign controlled_inverter_6_out = or_1_out ? ~controlled_buffer_1_out[6] : 1'bz;  // Controlled_Inverter controlled_inverter_6
  buf buffer_8 (buffer_8_out, controlled_buffer_1_out[3]);
  S_R_Flip_Flop s_r_ff_7 (.Q(Q[3]), .reset(controlled_inverter_7_out), .preset(buffer_8_out));  // open: S, R, clk, Qn
  assign controlled_inverter_7_out = or_1_out ? ~controlled_buffer_1_out[3] : 1'bz;  // Controlled_Inverter controlled_inverter_7
  buf buffer_9 (buffer_9_out, controlled_buffer_1_out[7]);
  S_R_Flip_Flop s_r_ff_8 (.Q(Q[7]), .reset(controlled_inverter_8_out), .preset(buffer_9_out));  // open: S, R, clk, Qn
  assign controlled_inverter_8_out = or_1_out ? ~controlled_buffer_1_out[7] : 1'bz;  // Controlled_Inverter controlled_inverter_8
endmodule
