// Logisim project latchw.circ as structural Verilog: 1 circuit, main circuit LATCH16
module LATCH16 (
  input  WE,
  input  R,
  input  [15:0] D,
  output [15:0] Q
);

  wire and_1_out, buffer_2_out, buffer_3_out, buffer_4_out, buffer_5_out, buffer_6_out, buffer_7_out,
       buffer_8_out, buffer_9_out, buffer_10_out, buffer_11_out, buffer_12_out, buffer_13_out, buffer_14_out,
       buffer_15_out, buffer_16_out, buffer_17_out, controlled_inverter_1_out, controlled_inverter_2_out,
       controlled_inverter_3_out, controlled_inverter_4_out, controlled_inverter_5_out,
       controlled_inverter_6_out, controlled_inverter_7_out, controlled_inverter_8_out,
       controlled_inverter_9_out, controlled_inverter_10_out, controlled_inverter_11_out,
       controlled_inverter_12_out, controlled_inverter_13_out, controlled_inverter_14_out,
       controlled_inverter_15_out, controlled_inverter_16_out, or_1_out;
  wire [15:0] buffer_1_out, controlled_buffer_1_out;

  and and_1 (and_1_out, WE, ~R);  // AND_Gate
  assign buffer_1_out = D;  // Buffer buffer_1, 16 bits wide
  or or_1 (or_1_out, WE, R);
  assign controlled_buffer_1_out = and_1_out ? buffer_1_out : 16'bz;  // Controlled_Buffer controlled_buffer_1
  assign controlled_buffer_1_out = R ? {16{1'b0}} : 16'bz;  // Controlled_Buffer controlled_buffer_2
  buf buffer_2 (buffer_2_out, controlled_buffer_1_out[0]);
  S_R_Flip_Flop s_r_ff_1 (.Q(Q[0]), .reset(controlled_inverter_1_out), .preset(buffer_2_out));  // open: S, R, clk, Qn
  buf buffer_3 (buffer_3_out, controlled_buffer_1_out[8]);
  S_R_Flip_Flop s_r_ff_2 (.Q(Q[8]), .reset(controlled_inverter_2_out), .preset(buffer_3_out));  // open: S, R, clk, Qn
  S_R_Flip_Flop s_r_ff_3 (.Q(Q[1]), .reset(controlled_inverter_3_out), .preset(buffer_4_out));  // open: S, R, clk, Qn
  assign controlled_inverter_1_out = or_1_out ? ~controlled_buffer_1_out[0] : 1'bz;  // Controlled_Inverter controlled_inverter_1
  S_R_Flip_Flop s_r_ff_4 (.Q(Q[9]), .reset(controlled_inverter_4_out), .preset(buffer_5_out));  // open: S, R, clk, Qn
  assign controlled_inverter_2_out = or_1_out ? ~controlled_buffer_1_out[8] : 1'bz;  // Controlled_Inverter controlled_inverter_2
  buf buffer_4 (buffer_4_out, controlled_buffer_1_out[1]);
  assign controlled_inverter_3_out = or_1_out ? ~controlled_buffer_1_out[1] : 1'bz;  // Controlled_Inverter controlled_inverter_3
  buf buffer_5 (buffer_5_out, controlled_buffer_1_out[9]);
  assign controlled_inverter_4_out = or_1_out ? ~controlled_buffer_1_out[9] : 1'bz;  // Controlled_Inverter controlled_inverter_4
  buf buffer_6 (buffer_6_out, controlled_buffer_1_out[2]);
  S_R_Flip_Flop s_r_ff_5 (.Q(Q[2]), .reset(controlled_inverter_5_out), .preset(buffer_6_out));  // open: S, R, clk, Qn
  assign controlled_inverter_5_out = or_1_out ? ~controlled_buffer_1_out[2] : 1'bz;  // Controlled_Inverter controlled_inverter_5
  buf buffer_7 (buffer_7_out, controlled_buffer_1_out[10]);
  S_R_Flip_Flop s_r_ff_6 (.Q(Q[10]), .reset(controlled_inverter_6_out), .preset(buffer_7_out));  // open: S, R, clk, Qn
  assign controlled_inverter_6_out = or_1_out ? ~controlled_buffer_1_out[10] : 1'bz;  // Controlled_Inverter controlled_inverter_6
  buf buffer_8 (buffer_8_out, controlled_buffer_1_out[3]);
  S_R_Flip_Flop s_r_ff_7 (.Q(Q[3]), .reset(controlled_inverter_7_out), .preset(buffer_8_out));  // open: S, R, clk, Qn
  assign controlled_inverter_7_out = or_1_out ? ~controlled_buffer_1_out[3] : 1'bz;  // Controlled_Inverter controlled_inverter_7
  buf buffer_9 (buffer_9_out, controlled_buffer_1_out[11]);
  S_R_Flip_Flop s_r_ff_8 (.Q(Q[11]), .reset(controlled_inverter_8_out), .preset(buffer_9_out));  // open: S, R, clk, Qn
  assign controlled_inverter_8_out = or_1_out ? ~controlled_buffer_1_out[11] : 1'bz;  // Controlled_Inverter controlled_inverter_8
  buf buffer_10 (buffer_10_out, controlled_buffer_1_out[4]);
  S_R_Flip_Flop s_r_ff_9 (.Q(Q[4]), .reset(controlled_inverter_9_out), .preset(buffer_10_out));  // open: S, R, clk, Qn
  assign controlled_inverter_9_out = or_1_out ? ~controlled_buffer_1_out[4] : 1'bz;  // Controlled_Inverter controlled_inverter_9
  buf buffer_11 (buffer_11_out, controlled_buffer_1_out[12]);
  S_R_Flip_Flop s_r_ff_10 (
    .Q(Q[12]), .reset(controlled_inverter_10_out), .preset(buffer_11_out));  // open: S, R, clk, Qn
  assign controlled_inverter_10_out = or_1_out ? ~controlled_buffer_1_out[12] : 1'bz;  // Controlled_Inverter controlled_inverter_10
  buf buffer_12 (buffer_12_out, controlled_buffer_1_out[5]);
  S_R_Flip_Flop s_r_ff_11 (
    .Q(Q[5]), .reset(controlled_inverter_11_out), .preset(buffer_12_out));  // open: S, R, clk, Qn
  assign controlled_inverter_11_out = or_1_out ? ~controlled_buffer_1_out[5] : 1'bz;  // Controlled_Inverter controlled_inverter_11
  buf buffer_13 (buffer_13_out, controlled_buffer_1_out[13]);
  S_R_Flip_Flop s_r_ff_12 (
    .Q(Q[13]), .reset(controlled_inverter_12_out), .preset(buffer_13_out));  // open: S, R, clk, Qn
  assign controlled_inverter_12_out = or_1_out ? ~controlled_buffer_1_out[13] : 1'bz;  // Controlled_Inverter controlled_inverter_12
  buf buffer_14 (buffer_14_out, controlled_buffer_1_out[6]);
  S_R_Flip_Flop s_r_ff_13 (
    .Q(Q[6]), .reset(controlled_inverter_13_out), .preset(buffer_14_out));  // open: S, R, clk, Qn
  assign controlled_inverter_13_out = or_1_out ? ~controlled_buffer_1_out[6] : 1'bz;  // Controlled_Inverter controlled_inverter_13
  buf buffer_15 (buffer_15_out, controlled_buffer_1_out[14]);
  S_R_Flip_Flop s_r_ff_14 (
    .Q(Q[14]), .reset(controlled_inverter_14_out), .preset(buffer_15_out));  // open: S, R, clk, Qn
  assign controlled_inverter_14_out = or_1_out ? ~controlled_buffer_1_out[14] : 1'bz;  // Controlled_Inverter controlled_inverter_14
  buf buffer_16 (buffer_16_out, controlled_buffer_1_out[7]);
  S_R_Flip_Flop s_r_ff_15 (
    .Q(Q[7]), .reset(controlled_inverter_15_out), .preset(buffer_16_out));  // open: S, R, clk, Qn
  assign controlled_inverter_15_out = or_1_out ? ~controlled_buffer_1_out[7] : 1'bz;  // Controlled_Inverter controlled_inverter_15
  buf buffer_17 (buffer_17_out, controlled_buffer_1_out[15]);
  S_R_Flip_Flop s_r_ff_16 (
    .Q(Q[15]), .reset(controlled_inverter_16_out), .preset(buffer_17_out));  // open: S, R, clk, Qn
  assign controlled_inverter_16_out = or_1_out ? ~controlled_buffer_1_out[15] : 1'bz;  // Controlled_Inverter controlled_inverter_16
endmodule
