// Logisim project trigger.circ as structural Verilog: 1 circuit, main circuit trigger
module trigger (
  input  CLK,
  output Q
);

  wire buffer_1_out, buffer_2_out;

  D_Flip_Flop d_ff_1 (.D(1'b1), .clk(CLK), .Q(Q), .reset(buffer_2_out));  // open: Qn, preset
  buf buffer_1 (buffer_1_out, Q);
  buf buffer_2 (buffer_2_out, buffer_1_out);
endmodule
